# Fritzing sketch wiring (saved by Fritzing 0.9.3b)
breadboards: 1

parts:
  Composant1 = Arduino Nano (Rev3.0)
  hc-sr1 = hc-sr04
  VCC1 = Battery block 9V  # not connected
  J1 = Basic Servo

nets:
  N1: Composant1.D2, hc-sr1.Trig
  N2: Composant1.D3, hc-sr1.Echo
  GND: Composant1.GND, hc-sr1.GND, J1.gnd
  VCC: Composant1.5V, hc-sr1.VCC, J1.vcc
